# Fritzing sketch sketch (saved by Fritzing 0.9.3b)
breadboards: 3

parts:
  BT1 = Bluetooth HC-06u [package=THT]
  부품1 = Arduino Uno (Rev3)
  M1 = DC Motor
  M2 = DC Motor
  Power_plug1 = Power plug [part_number="12V 2A"]
  Part1 = KY-015 Temperature & Humidity Sensor Module [package="Breakout board"]
  DFRobot_DFPlayer_Mini1 = DFRobot DFPlayer Mini [part_number=DFR0299]
  R1 = Resistor [tolerance=±5% resistance=1k package=THT]
  부품5 = ws2812b [package="smd 2812b"]
  부품3 = ws2812b [package="smd 2812b"]
  부품2 = ws2812b [package="smd 2812b"]
  S1 = H-Bridge with L298N
  부품4 = ws2812b [package="smd 2812b"]
  SPKR1 = Loudspeaker
  FC-1 = Sound Sensor

nets:
  VDD: BT1.VCC, 부품1.5V, Part1.Vin, DFRobot_DFPlayer_Mini1.VCC, 부품5.VDD, 부품3.VDD, 부품2.VDD, 부품4.VDD, FC-1.VCC
  GND: BT1.GND, 부품1.GND, Power_plug1.GND, Part1.-, DFRobot_DFPlayer_Mini1.GND-1, DFRobot_DFPlayer_Mini1.GND-2, 부품5.VSS, 부품3.VSS, 부품2.VSS, S1.GND, 부품4.VSS, FC-1.GND
  N1: BT1.TXD, 부품1.D2
  N2: BT1.RXD, 부품1.D3_PWM
  N3: 부품1.A0, FC-1.OUT
  N4: 부품1.D8, DFRobot_DFPlayer_Mini1.TX
  N5: 부품1.D9_PWM, R1.Pin_1
  N6: 부품1.D10_PWM/SS, DFRobot_DFPlayer_Mini1.BUSY
  N7: 부품1.D11_PWM/MOSI, S1.IN3
  N8: 부품1.D12/MISO, S1.IN4
  N9: 부품1.D4, Part1.S
  N10: 부품1.D5_PWM, 부품4.DIN
  N11: 부품1.D6_PWM, S1.IN1
  N12: 부품1.D7, S1.IN2
  N13: M1.pin_1, S1.M1-01
  N14: M1.pin_2, S1.M1-02
  N15: M2.pin_1, S1.M2-02
  N16: M2.pin_2, S1.M2-01
  VCC: Power_plug1.VCC, S1.12V
  N17: DFRobot_DFPlayer_Mini1.RX, R1.Pin_0
  N18: DFRobot_DFPlayer_Mini1.SPK_1, SPKR1.pin2
  N19: DFRobot_DFPlayer_Mini1.SPK_2, SPKR1.pin1
  N20: 부품5.DIN, 부품2.DOUT
  N21: 부품3.DOUT, 부품2.DIN
  N22: 부품3.DIN, 부품4.DOUT

custom parts:
  Bluetooth HC-06u: Bluetooth HC-06 - face up, pins down 16.5mm x 37.5mm PCB
  KY-015 Temperature & Humidity Sensor Module: KY-015 temperature and humidity sensor module, provides a low-latency serial interface to measure humidity and temperature.
  H-Bridge with L298N: h-bridge
